# Fritzing sketch wobble (saved by Fritzing 0.9.2b)
breadboards: 1

parts:
  Part1 = Arduino Nano (Rev3.0)
  Part2 = Triple Axis Accelerometer Breakout - ADXL335

nets:
  N1: Part1.RESET, Part2.ST
  GND: Part1.GND, Part2.GND
  5V: Part1.5V, Part2.VCC
  N2: Part1.A1, Part1.A0, Part2.XOUT
